# Fritzing sketch OCB Radio (saved by Fritzing 0.9.3b)
circuit board: 8.46667cm x 5.64444cm
circuit board: 7.10859cm x 2.0229cm
breadboards: 3

parts:
  Arduino_Mega_2560 = Arduino Mega 2560 (Rev3)
  RE1 = Rotary Encoder [package=THT]
  S2 = Pushbutton [package="[THT]"]
  S3 = Pushbutton [package="[THT]"]
  U1 = POT_SWITCH [package=pot_pth_switch]  # not connected
  U2 = SI470X [package=si470x]  # not connected
  R1 = Resistor [tolerance=±5% resistance=10k package=THT]
  R2 = Resistor [tolerance=±5% resistance=10k package=THT]
  R4 = Resistor [tolerance=±5% resistance=10k package=THT]
  R5 = Resistor [tolerance=±5% resistance=10k package=THT]
  DFRobot_DFPlayer_Mini1 = DFRobot DFPlayer Mini [part_number=DFR0299]
  TRS1 = Audio Jack (TRS) 3.5mm [package="4Ucon 08780 [THT]"]  # not connected
  S4 = Pushbutton [package="[THT]"]
  U3 = USB Connectors [package=usb-a-s-nosilk]  # not connected
  U4 = 2-Channel 5v Relay Shield [package=relay-2ch5v10a]  # not connected

nets:
  N1: Arduino_Mega_2560.A2, RE1.EncoderPinB
  N2: Arduino_Mega_2560.A3, RE1.EncoderPinA
  N3: S2.Pin_3, S2.Pin_4, R2.Pin_1
  N4: S3.Pin_4, R1.Pin_1
  N5: R1.Pin_0, R2.Pin_0, R5.Pin_0
  N6: R4.Pin_0, S4.Pin_1, S4.Pin_2
  N7: R5.Pin_1, S4.Pin_3, S4.Pin_4
  N8: DFRobot_DFPlayer_Mini1.GND-1, DFRobot_DFPlayer_Mini1.GND-2

custom parts:
  DFRobot DFPlayer Mini: The DFPlayer Mini is a small and low cost MP3 module with an simplified output directly to the speaker. The module can be used as a stand alone module with attached battery, speaker and push buttons or used in combination with an Arduino UNO or any other with RX/TX capabilities.
  2-Channel 5v Relay Shield: 2 Channel 5v Relay Shield w. 2x SPD-06VDC-SD-C
